# Fritzing sketch Circuit (saved by Fritzing 0.9.3b)

parts:
  Componente1 = Arduino Nano (Rev3.0) (ICSP)
  Display1 = LCD screen 16x2 IIC [part_number=101290]
  Arriba_izquierda = KY-018 Photoresistor Module [package="Breakout board"]
  Arriba_derecha = KY-018 Photoresistor Module [package="Breakout board"]
  Abajo_izquierda = KY-018 Photoresistor Module [package="Breakout board"]
  Abajo_derecha = KY-018 Photoresistor Module [package="Breakout board"]
  Componente2 = ACS712 Current Sensor Module
  M1 = MT3608 Module
  X1 = USB Connectors [package=usb-a-s]
  BATT1 = LiPoly Battery (1300mAh)
  Vertical = Basic Servo
  Horizontal = Basic Servo
  Mod1 = Nano-V3-0-IO-Expansion-Adapter
  TP1 = TP4056 [chip_label=TP4056 package="DIP (Dual Inline) [THT]"]
  Componente3 = Solar Cell
  Componente4 = Solar Cell
  S3 = SWITCH-MOMENTARY-2 [package=tactile-pth]

nets (from the breadboard view):
  N1: Componente1.D1/TX, Mod1.D1/TX#65
  N2: Componente1.D0/RX, Display1.GND, Mod1.D0/RX, Mod1.D1/TX#79
  N3: Componente1.RESET, Componente1.A0, Arriba_izquierda.S, Mod1.RST, Mod1.A0
  GND: Componente1.GND, Componente1.D6, Componente1.A3, Arriba_izquierda.-, Arriba_derecha.-, Abajo_izquierda.-, Abajo_derecha.S, Abajo_derecha.-, Componente2.GND, Vertical.gnd, Horizontal.gnd, Horizontal.pulse, Mod1.GND, Mod1.A3, Mod1.D6_PWM
  N4: Componente1.D2, Mod1.D2
  N5: Componente1.D3, Mod1.D3_PWM
  N6: Componente1.D4, Mod1.D4
  N7: Componente1.D5, Vertical.pulse, Mod1.D5_PWM
  N8: Componente1.D7, Mod1.D7
  N9: Componente1.D8, Mod1.D8
  N10: Componente1.D9, Mod1.D9_PWM
  N11: Componente1.D10, Mod1.D10_PWM/SS
  N12: Componente1.D11/MOSI, Mod1.D11_PWM/MOSI
  N13: Componente1.D12/MISO, Mod1.D12/MISO
  VIN: Componente1.VIN, Mod1.VIN
  VCC: Componente1.5V, Componente1.A2, Display1.VCC, Arriba_izquierda.Vin, Arriba_derecha.Vin, Abajo_izquierda.S, Abajo_izquierda.Vin, Abajo_derecha.Vin, Componente2.VCC, Vertical.vcc, Horizontal.vcc, Mod1.VCC, Mod1.A2
  N14: Componente1.A7, Mod1.A7
  N15: Componente1.A6, Componente2.OUT, Mod1.A6
  N16: Componente1.A5, Display1.SCL, Mod1.A5/SCL
  N17: Componente1.A4, Display1.SDA, Mod1.A4/SDA
  N18: Componente1.A1, Arriba_derecha.S, Mod1.NC/3V3, Mod1.A1
  N19: Componente1.AREF, Mod1.AREF
  N20: Componente1.3V3, Mod1.NC
  N21: Componente1.D13/SCK, Mod1.D13/SCK
  N22: Componente2.INPUT+, Componente3.+, Componente4.+
  N23: Componente2.INPUT-, TP1.pin1
  N24: M1.pin1, S3.1
  N25: M1.pin2, TP1.pin3
  N26: M1.pin3, X1.VBUS
  N27: M1.pin4, X1.GND
  N28: BATT1.positive, TP1.pin4
  N29: BATT1.negative, TP1.pin5
  N30: TP1.pin2, Componente3.-, Componente4.-
  N31: TP1.pin6, S3.2

custom parts:
  LCD screen 16x2 IIC: LCD screen with HD44780 controller enables showing text, symbols, value or anything else that comes from Croduino/Arduino. It is capable of showing 16 symbols in two lines and therefore can be used in many projects that need to send clearly visible and legible output information.. • Color of symbols: White • Backlight: Blue • Dimensions: 80 x 36 x 12 mm • Screen dimensions: 64.5 x 16 mm •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
  KY-018 Photoresistor Module: KY-018 Photoresistor module, used to measure light intensity. It can determine the presence or absence of light.
  MT3608 Module: MT3608 Boost Converter Module Links: Aerosemi MT3608 2A Step Up Converter datasheet
  LiPoly Battery (1300mAh): Lithium Ion Polymer Battery (1300mAh)
  Nano-V3-0-IO-Expansion-Adapter: Nano V3.0 IO Expansion Adapter Shield. Note pcb view has been supressed as not useful. You can drag a Nano over the Nano connectors and it will connect and appear in schematic (although at present due to a bug, routing will not show as complete in breadboard).
  TP4056: A DIP stand-in part for whatever IC you want. With 6 pins on a 300mil dual inline package (DIP) footprint.
